// Logisim project mainCPU.circ as structural Verilog: 6 circuits, main circuit main
module main (
);

  wire and_1_out, and_2_out, and_3_out, and_4_out, and_5_out, and_6_out, button_1_out, clock_1_out, d_ff_1_q,
       d_ff_2_q, d_ff_3_q, d_ff_4_q, d_ff_5_q, d_ff_6_q, d_ff_7_q, jump_1_out_4, mycirc_1_ex_mux,
       mycirc_1_mem_load, mycirc_1_mem_mux, mycirc_1_pc_update, mycirc_1_wb, mycirc_1_wb_data, not_1_out,
       not_2_out, or_1_out, register_1_q, xnor_1_out;
  wire [1:0] mycirc_1_wb_addr;
  wire [2:0] mycirc_1_ex_alu;
  wire [3:0] iCode_q, multiplexer_1_out, rA_q, rB_q;
  wire [7:0] ALU_val_e, counter_1_q, multiplexer_2_out, multiplexer_3_out, multiplexer_4_out,
       multiplexer_5_out, PC_q, ram_1_data, Register_File_r_out_1, Register_File_r_out_2, valA_q, valB_q,
       valC_q, valE_q, valM_q, valP_q;
  wire [15:0] rom_1_data;

  Register #(.width(1)) register_1 (.D(and_2_out), .Q(register_1_q), .clk(clock_1_out), .clr(and_4_out));  // open: en
  not not_1 (not_1_out, register_1_q);
  and and_1 (and_1_out, or_1_out, not_1_out);
  Clock clock_1 (.out(clock_1_out));
  Button button_1 (.out(button_1_out));
  and and_2 (and_2_out, iCode_q[3], iCode_q[2], iCode_q[1], iCode_q[0]);
  Register PC (.D(multiplexer_5_out), .en(and_1_out), .Q(PC_q), .clk(clock_1_out), .clr(and_3_out));
  and and_3 (and_3_out, and_4_out, not_1_out);
  D_Flip_Flop d_ff_1 (.clk(clock_1_out), .D(button_1_out), .Q(d_ff_1_q));  // open: Qn, preset, en, reset
  not not_2 (not_2_out, d_ff_1_q);
  and and_4 (and_4_out, not_2_out, button_1_out);
  or or_1 (or_1_out, and_4_out, d_ff_7_q, xnor_1_out);
  NotExactlyOne xnor_1 (
    .out(xnor_1_out), .in0(d_ff_3_q), .in1(d_ff_4_q), .in3(d_ff_5_q), .in4(d_ff_6_q), .in5(d_ff_7_q));
  ROM #(.dataWidth(16)) rom_1 (.addr(PC_q), .data(rom_1_data));  // open: sel
  D_Flip_Flop d_ff_2 (.clk(clock_1_out), .D(or_1_out), .Q(d_ff_2_q));  // open: Qn, preset, en, reset
  D_Flip_Flop d_ff_3 (.clk(clock_1_out), .D(d_ff_2_q), .Q(d_ff_3_q));  // open: Qn, preset, en, reset
  Counter counter_1 (.D(PC_q), .Q(counter_1_q), .clk(d_ff_7_q), .clr(and_4_out));  // open: load, count, carry
  Register #(.width(4)) iCode (.D(rom_1_data[15:12]), .en(d_ff_2_q), .Q(iCode_q), .clk(clock_1_out));  // open: clr
  Register #(.width(4)) rA (.D(rom_1_data[11:8]), .en(d_ff_2_q), .Q(rA_q), .clk(clock_1_out));  // open: clr
  Register #(.width(4)) rB (.D(rom_1_data[7:4]), .en(d_ff_2_q), .Q(rB_q), .clk(clock_1_out));  // open: clr
  Register valC (.D(rom_1_data[7:0]), .en(d_ff_2_q), .Q(valC_q), .clk(clock_1_out));  // open: clr
  Register valP (.D(counter_1_q), .en(d_ff_2_q), .Q(valP_q), .clk(clock_1_out), .clr(and_4_out));
  D_Flip_Flop d_ff_4 (.clk(clock_1_out), .D(d_ff_3_q), .Q(d_ff_4_q), .reset(xnor_1_out));  // open: Qn, preset, en
  Multiplexer #(.select(2), .width(4), .enable("false")) multiplexer_1 (
    .in0(rA_q), .in1(rB_q), .in2(4'b0000), .in3(4'b0000), .out(multiplexer_1_out), .sel(mycirc_1_wb_addr));
  and and_5 (and_5_out, d_ff_7_q, mycirc_1_wb);
  myCirc mycirc_1 (
    .in_1(iCode_q), .wb_addr(mycirc_1_wb_addr), .wb_data(mycirc_1_wb_data), .ex_mux(mycirc_1_ex_mux),
    .mem_mux(mycirc_1_mem_mux), .mem_load(mycirc_1_mem_load), .ex_alu(mycirc_1_ex_alu),
    .pc_update(mycirc_1_pc_update), .wb(mycirc_1_wb));
  Register_File Register_File (
    .w_data(multiplexer_2_out), .e_2(and_5_out), .w_addr(multiplexer_1_out), .e(d_ff_4_q), .r_addr_1(rA_q),
    .r_out_1(Register_File_r_out_1), .r_out_2(Register_File_r_out_2), .e_3(d_ff_4_q), .r_addr_1_2(rB_q),
    .in_6(clock_1_out), .in_7(and_4_out));
  Multiplexer #(.width(8), .enable("false")) multiplexer_2 (
    .in0(valE_q), .in1(valM_q), .out(multiplexer_2_out), .sel(mycirc_1_wb_data));
  Register valA (.D(Register_File_r_out_1), .en(d_ff_4_q), .Q(valA_q), .clk(clock_1_out));  // open: clr
  Register valB (.D(Register_File_r_out_2), .en(d_ff_4_q), .Q(valB_q), .clk(clock_1_out));  // open: clr
  D_Flip_Flop d_ff_5 (.clk(clock_1_out), .D(d_ff_4_q), .Q(d_ff_5_q), .reset(xnor_1_out));  // open: Qn, preset, en
  Multiplexer #(.width(8), .enable("false")) multiplexer_3 (
    .in0(valC_q), .in1(valA_q), .out(multiplexer_3_out), .sel(mycirc_1_ex_mux));
  ALU ALU (.A(multiplexer_3_out), .B(valB_q), .ALU_fun(mycirc_1_ex_alu), .val_E(ALU_val_e));
  Register valE (.D(ALU_val_e), .en(d_ff_5_q), .Q(valE_q), .clk(clock_1_out));  // open: clr
  D_Flip_Flop d_ff_6 (.clk(clock_1_out), .D(d_ff_5_q), .Q(d_ff_6_q), .reset(xnor_1_out));  // open: Qn, preset, en
  Multiplexer #(.width(8), .enable("false")) multiplexer_4 (
    .in0(valE_q), .in1(valA_q), .out(multiplexer_4_out), .sel(mycirc_1_mem_mux));
  and and_6 (and_6_out, mycirc_1_mem_mux, d_ff_6_q);
  RAM #(.bus("separate")) ram_1 (
    .addr(multiplexer_4_out), .din(valE_q), .data(ram_1_data), .str(and_6_out), .clk(clock_1_out),
    .ld(mycirc_1_mem_load), .clr(and_4_out));  // open: sel
  D_Flip_Flop d_ff_7 (.clk(clock_1_out), .D(d_ff_6_q), .Q(d_ff_7_q), .reset(xnor_1_out));  // open: Qn, preset, en
  jump jump_1 (.jmp_mux(mycirc_1_pc_update), .code(iCode_q), .value(valA_q), .out_4(jump_1_out_4));
  Register valM (.D(ram_1_data), .en(d_ff_6_q), .Q(valM_q), .clk(clock_1_out));  // open: clr
  Multiplexer #(.width(8), .enable("false")) multiplexer_5 (
    .in0(valE_q), .in1(valP_q), .out(multiplexer_5_out), .sel(jump_1_out_4));

  // Notes on the sheet:
  //   Fetch
  //   contents of rom_1 (hex, n*v repeats v):
  //   2101 2202 2303 2404 2504 2603 2702 2801 3190 32a0 33b0 34c0 1590 16a0 17b0 18c0 4090 41a0 42b0 43c0
  //   5000 7f20 10*0 6030 15*0 f000
  //   Decode
  //   Write Back
  //   Execute
  //   Memory
  //   PC Update
endmodule

module Register_File (
  input  [7:0] w_data,
  input  [3:0] r_addr_1,
  input  e,
  input  e_2,
  input  [3:0] w_addr,
  input  in_6,
  input  in_7,
  input  e_3,
  input  [3:0] r_addr_1_2,
  output [7:0] r_out_1,
  output [7:0] r_out_2
);

  wire and_1_out, and_2_out, and_3_out, and_4_out, and_5_out, and_6_out, and_7_out, and_8_out, and_9_out,
       and_10_out, and_11_out, and_12_out, and_13_out, and_14_out, and_15_out, and_16_out,
       demultiplexer_1_out0, demultiplexer_1_out1, demultiplexer_1_out2, demultiplexer_1_out3,
       demultiplexer_1_out4, demultiplexer_1_out5, demultiplexer_1_out6, demultiplexer_1_out7,
       demultiplexer_1_out8, demultiplexer_1_out9, demultiplexer_1_out10, demultiplexer_1_out11,
       demultiplexer_1_out12, demultiplexer_1_out13, demultiplexer_1_out14, demultiplexer_1_out15,
       demultiplexer_2_out0, demultiplexer_2_out1, demultiplexer_2_out2, demultiplexer_2_out3,
       demultiplexer_2_out4, demultiplexer_2_out5, demultiplexer_2_out6, demultiplexer_2_out7,
       demultiplexer_2_out8, demultiplexer_2_out9, demultiplexer_2_out10, demultiplexer_2_out11,
       demultiplexer_2_out12, demultiplexer_2_out13, demultiplexer_2_out14, demultiplexer_2_out15,
       demultiplexer_3_out0, demultiplexer_3_out1, demultiplexer_3_out2, demultiplexer_3_out3,
       demultiplexer_3_out4, demultiplexer_3_out5, demultiplexer_3_out6, demultiplexer_3_out7,
       demultiplexer_3_out8, demultiplexer_3_out9, demultiplexer_3_out10, demultiplexer_3_out11,
       demultiplexer_3_out12, demultiplexer_3_out13, demultiplexer_3_out14, demultiplexer_3_out15;
  wire [7:0] _0_q, _1_q, _2_q, _3_q, _4_q, _5_q, _6_q, _7_q, _8_q, _9_q, a_q, b_q, c_q, d_q, e_q, f_q;

  Demultiplexer #(.select(4)) demultiplexer_1 (
    .out0(demultiplexer_1_out0), .out1(demultiplexer_1_out1), .out2(demultiplexer_1_out2),
    .out3(demultiplexer_1_out3), .out4(demultiplexer_1_out4), .out5(demultiplexer_1_out5),
    .out6(demultiplexer_1_out6), .out7(demultiplexer_1_out7), .out8(demultiplexer_1_out8),
    .out9(demultiplexer_1_out9), .out10(demultiplexer_1_out10), .out11(demultiplexer_1_out11),
    .out12(demultiplexer_1_out12), .out13(demultiplexer_1_out13), .out14(demultiplexer_1_out14),
    .out15(demultiplexer_1_out15), .in(1'b1), .sel(w_addr));  // open: en
  and and_1 (and_1_out, demultiplexer_1_out0, e_2);
  and and_2 (and_2_out, demultiplexer_1_out1, e_2);
  and and_3 (and_3_out, demultiplexer_1_out2, e_2);
  and and_4 (and_4_out, demultiplexer_1_out3, e_2);
  and and_5 (and_5_out, demultiplexer_1_out4, e_2);
  and and_6 (and_6_out, demultiplexer_1_out5, e_2);
  and and_7 (and_7_out, demultiplexer_1_out6, e_2);
  and and_8 (and_8_out, demultiplexer_1_out7, e_2);
  and and_9 (and_9_out, demultiplexer_1_out8, e_2);
  and and_10 (and_10_out, demultiplexer_1_out9, e_2);
  and and_11 (and_11_out, demultiplexer_1_out10, e_2);
  and and_12 (and_12_out, demultiplexer_1_out11, e_2);
  and and_13 (and_13_out, demultiplexer_1_out12, e_2);
  and and_14 (and_14_out, demultiplexer_1_out13, e_2);
  and and_15 (and_15_out, demultiplexer_1_out14, e_2);
  and and_16 (and_16_out, demultiplexer_1_out15, e_2);
  Register _0 (.D(w_data), .en(and_1_out), .Q(_0_q), .clk(in_6), .clr(in_7));
  Register _1 (.D(w_data), .en(and_2_out), .Q(_1_q), .clk(in_6), .clr(in_7));
  Register _2 (.D(w_data), .en(and_3_out), .Q(_2_q), .clk(in_6), .clr(in_7));
  Register _3 (.D(w_data), .en(and_4_out), .Q(_3_q), .clk(in_6), .clr(in_7));
  Register _4 (.D(w_data), .en(and_5_out), .Q(_4_q), .clk(in_6), .clr(in_7));
  Register _5 (.D(w_data), .en(and_6_out), .Q(_5_q), .clk(in_6), .clr(in_7));
  Register _6 (.D(w_data), .en(and_7_out), .Q(_6_q), .clk(in_6), .clr(in_7));
  Register _7 (.D(w_data), .en(and_8_out), .Q(_7_q), .clk(in_6), .clr(in_7));
  Register _8 (.D(w_data), .en(and_9_out), .Q(_8_q), .clk(in_6), .clr(in_7));
  Register _9 (.D(w_data), .en(and_10_out), .Q(_9_q), .clk(in_6), .clr(in_7));
  Register a (.D(w_data), .en(and_11_out), .Q(a_q), .clk(in_6), .clr(in_7));
  Register b (.D(w_data), .en(and_12_out), .Q(b_q), .clk(in_6), .clr(in_7));
  Register c (.D(w_data), .en(and_13_out), .Q(c_q), .clk(in_6), .clr(in_7));
  Register d (.D(w_data), .en(and_14_out), .Q(d_q), .clk(in_6), .clr(in_7));
  Register u_e (.D(w_data), .en(and_15_out), .Q(e_q), .clk(in_6), .clr(in_7));
  Register f (.D(w_data), .en(and_16_out), .Q(f_q), .clk(in_6), .clr(in_7));
  assign r_out_1 = demultiplexer_2_out0 ? _0_q : 8'bz;  // Controlled_Buffer controlled_buffer_1
  assign r_out_2 = demultiplexer_3_out0 ? _0_q : 8'bz;  // Controlled_Buffer controlled_buffer_2
  assign r_out_1 = demultiplexer_2_out1 ? _1_q : 8'bz;  // Controlled_Buffer controlled_buffer_3
  assign r_out_2 = demultiplexer_3_out1 ? _1_q : 8'bz;  // Controlled_Buffer controlled_buffer_4
  assign r_out_1 = demultiplexer_2_out2 ? _2_q : 8'bz;  // Controlled_Buffer controlled_buffer_5
  assign r_out_2 = demultiplexer_3_out2 ? _2_q : 8'bz;  // Controlled_Buffer controlled_buffer_6
  assign r_out_1 = demultiplexer_2_out3 ? _3_q : 8'bz;  // Controlled_Buffer controlled_buffer_7
  assign r_out_2 = demultiplexer_3_out3 ? _3_q : 8'bz;  // Controlled_Buffer controlled_buffer_8
  assign r_out_1 = demultiplexer_2_out4 ? _4_q : 8'bz;  // Controlled_Buffer controlled_buffer_9
  assign r_out_2 = demultiplexer_3_out4 ? _4_q : 8'bz;  // Controlled_Buffer controlled_buffer_10
  assign r_out_1 = demultiplexer_2_out5 ? _5_q : 8'bz;  // Controlled_Buffer controlled_buffer_11
  assign r_out_2 = demultiplexer_3_out5 ? _5_q : 8'bz;  // Controlled_Buffer controlled_buffer_12
  assign r_out_1 = demultiplexer_2_out6 ? _6_q : 8'bz;  // Controlled_Buffer controlled_buffer_13
  assign r_out_2 = demultiplexer_3_out6 ? _6_q : 8'bz;  // Controlled_Buffer controlled_buffer_14
  assign r_out_1 = demultiplexer_2_out7 ? _7_q : 8'bz;  // Controlled_Buffer controlled_buffer_15
  assign r_out_2 = demultiplexer_3_out7 ? _7_q : 8'bz;  // Controlled_Buffer controlled_buffer_16
  assign r_out_1 = demultiplexer_2_out8 ? _8_q : 8'bz;  // Controlled_Buffer controlled_buffer_17
  assign r_out_2 = demultiplexer_3_out8 ? _8_q : 8'bz;  // Controlled_Buffer controlled_buffer_18
  assign r_out_1 = demultiplexer_2_out9 ? _9_q : 8'bz;  // Controlled_Buffer controlled_buffer_19
  assign r_out_2 = demultiplexer_3_out9 ? _9_q : 8'bz;  // Controlled_Buffer controlled_buffer_20
  assign r_out_1 = demultiplexer_2_out10 ? a_q : 8'bz;  // Controlled_Buffer controlled_buffer_21
  assign r_out_2 = demultiplexer_3_out10 ? a_q : 8'bz;  // Controlled_Buffer controlled_buffer_22
  assign r_out_1 = demultiplexer_2_out11 ? b_q : 8'bz;  // Controlled_Buffer controlled_buffer_23
  assign r_out_2 = demultiplexer_3_out11 ? b_q : 8'bz;  // Controlled_Buffer controlled_buffer_24
  assign r_out_1 = demultiplexer_2_out12 ? c_q : 8'bz;  // Controlled_Buffer controlled_buffer_25
  assign r_out_2 = demultiplexer_3_out12 ? c_q : 8'bz;  // Controlled_Buffer controlled_buffer_26
  assign r_out_1 = demultiplexer_2_out13 ? d_q : 8'bz;  // Controlled_Buffer controlled_buffer_27
  assign r_out_2 = demultiplexer_3_out13 ? d_q : 8'bz;  // Controlled_Buffer controlled_buffer_28
  assign r_out_1 = demultiplexer_2_out14 ? e_q : 8'bz;  // Controlled_Buffer controlled_buffer_29
  assign r_out_2 = demultiplexer_3_out14 ? e_q : 8'bz;  // Controlled_Buffer controlled_buffer_30
  assign r_out_1 = demultiplexer_2_out15 ? f_q : 8'bz;  // Controlled_Buffer controlled_buffer_31
  assign r_out_2 = demultiplexer_3_out15 ? f_q : 8'bz;  // Controlled_Buffer controlled_buffer_32
  Demultiplexer #(.select(4)) demultiplexer_2 (
    .out0(demultiplexer_2_out0), .out1(demultiplexer_2_out1), .out2(demultiplexer_2_out2),
    .out3(demultiplexer_2_out3), .out4(demultiplexer_2_out4), .out5(demultiplexer_2_out5),
    .out6(demultiplexer_2_out6), .out7(demultiplexer_2_out7), .out8(demultiplexer_2_out8),
    .out9(demultiplexer_2_out9), .out10(demultiplexer_2_out10), .out11(demultiplexer_2_out11),
    .out12(demultiplexer_2_out12), .out13(demultiplexer_2_out13), .out14(demultiplexer_2_out14),
    .out15(demultiplexer_2_out15), .in(1'b1), .sel(r_addr_1), .en(e));
  Demultiplexer #(.select(4)) demultiplexer_3 (
    .out0(demultiplexer_3_out0), .out1(demultiplexer_3_out1), .out2(demultiplexer_3_out2),
    .out3(demultiplexer_3_out3), .out4(demultiplexer_3_out4), .out5(demultiplexer_3_out5),
    .out6(demultiplexer_3_out6), .out7(demultiplexer_3_out7), .out8(demultiplexer_3_out8),
    .out9(demultiplexer_3_out9), .out10(demultiplexer_3_out10), .out11(demultiplexer_3_out11),
    .out12(demultiplexer_3_out12), .out13(demultiplexer_3_out13), .out14(demultiplexer_3_out14),
    .out15(demultiplexer_3_out15), .in(1'b1), .sel(r_addr_1_2), .en(e_3));
endmodule

module ALU (
  input  [7:0] A,
  input  [7:0] B,
  input  [2:0] ALU_fun,
  output [7:0] val_E
);

  wire [7:0] multiplexer_1_out, multiplexer_2_out, negator_1_out;

  Negator negator_1 (.in(A), .out(negator_1_out));
  Multiplexer #(.width(8)) multiplexer_1 (
    .in0(B), .in1({8{1'b0}}), .out(multiplexer_1_out), .sel(ALU_fun[2]));  // open: en
  Multiplexer #(.select(2), .width(8)) multiplexer_2 (
    .in0({8{1'b0}}), .in1(A), .in2(negator_1_out), .out(multiplexer_2_out), .sel(ALU_fun[1:0]));  // open: in3, en
  Adder adder_1 (.a(multiplexer_2_out), .b(multiplexer_1_out), .out(val_E));  // open: cin, cout
endmodule

module iCode (
  input  [3:0] in_1,
  output mem_addr_mux,
  output mem_addr_e,
  output mem_data_mux,
  output mem_data_e,
  output pc_mux,
  output wb_addr_mux,
  output wb_val_mux,
  output ex_val_mux,
  output [1:0] ex_alu_mux
);

  wire decoder_1_out1, decoder_1_out2, decoder_1_out3, decoder_1_out6, decoder_1_out7, or_2_out, or_3_out,
       or_6_out, wb_addr_e_out, wb_val_e_out;

  Decoder #(.select(4)) decoder_1 (
    .out1(decoder_1_out1), .out2(decoder_1_out2), .out3(decoder_1_out3), .out4(mem_data_e),
    .out5(mem_addr_mux), .out6(decoder_1_out6), .out7(decoder_1_out7), .sel(in_1));  // open: out0, out8, out9, out10, out11, out12, out13, out14, out15, en
  not not_1 (wb_addr_mux, decoder_1_out2);
  or wb_addr_e (wb_addr_e_out, decoder_1_out1, decoder_1_out2, decoder_1_out3, mem_addr_mux);
  or wb_val_e (wb_val_e_out, decoder_1_out1, decoder_1_out2, decoder_1_out3, mem_addr_mux);
  or or_1 (ex_val_mux, decoder_1_out1, decoder_1_out3, mem_data_e, mem_addr_mux);
  or or_2 (or_2_out, decoder_1_out1, decoder_1_out2, decoder_1_out3, mem_data_e, mem_addr_mux, decoder_1_out6, decoder_1_out7);
  or or_3 (or_3_out, decoder_1_out2, decoder_1_out3, mem_data_e, decoder_1_out6);
  // Priority_Encoder #(.select(2)) priority_encoder_1: pin names not known; wires that end beside it: or_2_out, or_3_out, decoder_1_out1, ex_alu_mux, decoder_1_out7
  // OR_Gate or_4 has open pins: in0=decoder_1_out1, in1=decoder_1_out2, in2=decoder_1_out3, in3=mem_data_e, in4=decoder_1_out6, in5=decoder_1_out7, out=open
  or or_5 (mem_addr_e, mem_data_e, mem_addr_mux);
  nor nor_1 (pc_mux, decoder_1_out6, decoder_1_out7);
  or or_6 (or_6_out, decoder_1_out1, decoder_1_out2, decoder_1_out3, mem_data_e, mem_addr_mux, decoder_1_out6, decoder_1_out7);

  assign mem_data_mux = mem_data_e;
  assign wb_val_mux = mem_addr_mux;
endmodule

module myCirc (
  input  [3:0] in_1,
  output wb,
  output [1:0] wb_addr,
  output wb_data,
  output ex_mux,
  output mem_mux,
  output mem_load,
  output [2:0] ex_alu,
  output pc_update
);

  wire and_1_out, and_2_out, and_3_out, and_4_out, and_5_out, and_7_out, and_8_out, and_11_out, and_12_out,
       and_13_out, and_14_out, and_15_out, and_16_out, and_17_out, and_18_out;

  and and_1 (and_1_out, ~in_1[0], ~in_1[1], in_1[2], ~in_1[3]);  // AND_Gate
  and and_2 (and_2_out, in_1[1], in_1[2], ~in_1[3]);  // AND_Gate
  and and_3 (and_3_out, in_1[0], ~in_1[1], ~in_1[3]);  // AND_Gate
  and and_4 (and_4_out, in_1[0], ~in_1[2], ~in_1[3]);  // AND_Gate
  and and_5 (and_5_out, in_1[0], in_1[1], in_1[2], ~in_1[3]);  // AND_Gate
  and and_6 (wb_data, in_1[0], ~in_1[1], in_1[2], ~in_1[3]);  // AND_Gate
  and and_7 (and_7_out, in_1[0], ~in_1[2], ~in_1[3]);  // AND_Gate
  and and_8 (and_8_out, ~in_1[0], ~in_1[1], in_1[2], ~in_1[3]);  // AND_Gate
  and and_9 (mem_mux, ~in_1[0], ~in_1[1], in_1[2], ~in_1[3]);  // AND_Gate
  and and_10 (mem_load, in_1[0], ~in_1[1], in_1[2], ~in_1[3]);  // AND_Gate
  and and_11 (and_11_out, in_1[1], ~in_1[2], ~in_1[3]);  // AND_Gate
  and and_12 (and_12_out, in_1[0], ~in_1[1], in_1[2], ~in_1[3]);  // AND_Gate
  and and_13 (and_13_out, ~in_1[0], in_1[1], in_1[2], ~in_1[3]);  // AND_Gate
  and and_14 (and_14_out, in_1[0], in_1[1], ~in_1[2], ~in_1[3]);  // AND_Gate
  and and_15 (and_15_out, ~in_1[2], ~in_1[3]);  // AND_Gate
  and and_16 (and_16_out, in_1[0], in_1[1], in_1[2], in_1[3]);
  and and_17 (and_17_out, ~in_1[1], in_1[2], ~in_1[3]);  // AND_Gate
  and and_18 (and_18_out, in_1[1], in_1[2], ~in_1[3]);  // AND_Gate
  nor nor_1 (wb, and_1_out, and_2_out);
  or or_1 (wb_addr[0], and_3_out, and_4_out);
  or or_2 (wb_addr[1], and_5_out, and_18_out);
  or or_3 (ex_alu[0], and_12_out, and_4_out, and_13_out, and_11_out, and_5_out);
  or or_4 (ex_alu[2], and_13_out, and_12_out, and_14_out, and_5_out);
  or or_5 (pc_update, and_15_out, and_16_out, and_17_out);
  or or_6 (ex_mux, and_7_out, and_8_out);

  assign ex_alu[1] = 1'b0;
endmodule

module jump (
  input  jmp_mux,
  input  [3:0] code,
  input  [7:0] value,
  output out_4
);

  wire and_1_out, and_2_out, and_3_out, and_4_out, nor_1_out;

  and and_1 (and_1_out, ~code[3], code[2], code[1], ~code[0]);  // AND_Gate
  and and_2 (and_2_out, code[0], code[1], code[2], ~code[3]);  // AND_Gate
  nor nor_1 (nor_1_out, value[0], value[1], value[2], value[3], value[4], value[5], value[6], value[7]);
  and and_3 (and_3_out, jmp_mux, ~and_1_out);  // AND_Gate
  and and_4 (and_4_out, ~and_2_out, jmp_mux, ~nor_1_out);  // AND_Gate
  or or_1 (out_4, and_3_out, and_4_out);
endmodule
