// Logisim project mainCPU1.circ as structural Verilog: 4 circuits, main circuit main
module main (
);

  wire and_1_out, clock_1_out, d_ff_1_q, d_ff_2_q, d_ff_3_q, d_ff_4_q, d_ff_5_q, mycirc_1_out_3,
       mycirc_1_out_4, mycirc_1_out_5, mycirc_1_out_6, mycirc_1_out_8, not_1_out, register_1_q;
  wire [1:0] mycirc_1_out_2;
  wire [2:0] mycirc_1_out_7;
  wire [3:0] iCode_q, multiplexer_1_out, rA_q, rB_q;
  wire [7:0] ALU_val_e, counter_1_q, multiplexer_2_out, multiplexer_3_out, multiplexer_4_out,
       multiplexer_5_out, PC_q, ram_1_data, Register_File_r_out_1, Register_File_r_out_2, valA_q, valB_q,
       valC_q, valE_q, valM_q, valP_q;
  wire [15:0] rom_1_data;

  Clock clock_1 (.out(clock_1_out));
  Register #(.width(1)) register_1 (.D(and_1_out), .Q(register_1_q), .clk(clock_1_out));  // open: en, clr
  not not_1 (not_1_out, register_1_q);
  Register PC (.D(multiplexer_5_out), .en(not_1_out), .Q(PC_q), .clk(clock_1_out), .clr(and_1_out));
  and and_1 (and_1_out, iCode_q[3], iCode_q[2], iCode_q[1], iCode_q[0]);
  ROM #(.dataWidth(16)) rom_1 (.addr(PC_q), .data(rom_1_data));  // open: sel
  Counter counter_1 (.D(PC_q), .Q(counter_1_q), .clk(clock_1_out));  // open: load, count, carry, clr
  Register #(.width(4)) iCode (.D(rom_1_data[3:0]), .Q(iCode_q), .clk(clock_1_out));  // open: en, clr
  Register #(.width(4)) rA (.D(rom_1_data[7:4]), .Q(rA_q), .clk(clock_1_out));  // open: en, clr
  Register #(.width(4)) rB (.D(rom_1_data[11:8]), .Q(rB_q), .clk(clock_1_out));  // open: en, clr
  Register valC (.D(rom_1_data[15:8]), .Q(valC_q), .clk(clock_1_out));  // open: en, clr
  D_Flip_Flop d_ff_1 (.clk(clock_1_out), .Q(d_ff_1_q));  // open: D, Qn, preset, en, reset
  Register valP (.D(counter_1_q), .Q(valP_q), .clk(clock_1_out));  // open: en, clr
  myCirc mycirc_1 (
    .in_1(iCode_q), .out_2(mycirc_1_out_2), .out_3(mycirc_1_out_3), .out_4(mycirc_1_out_4),
    .out_5(mycirc_1_out_5), .out_6(mycirc_1_out_6), .out_7(mycirc_1_out_7), .out_8(mycirc_1_out_8));
  Multiplexer #(.select(2), .width(4)) multiplexer_1 (
    .in0(rA_q), .in1(rB_q), .in2(4'b0000), .in3(4'b0000), .out(multiplexer_1_out), .sel(mycirc_1_out_2));  // open: en
  Multiplexer #(.width(8), .enable("false")) multiplexer_2 (
    .in0(valE_q), .in1(valM_q), .out(multiplexer_2_out), .sel(mycirc_1_out_3));
  Register_File Register_File (
    .w_data(multiplexer_2_out), .e_2(d_ff_5_q), .w_addr(multiplexer_1_out), .e(d_ff_1_q), .r_addr_1(rA_q),
    .r_out_1(Register_File_r_out_1), .r_out_2(Register_File_r_out_2), .e_3(d_ff_1_q), .r_addr_1_2(rB_q),
    .in_6(clock_1_out));
  D_Flip_Flop d_ff_2 (.clk(clock_1_out), .D(d_ff_1_q), .Q(d_ff_2_q));  // open: Qn, preset, en, reset
  Register valA (.D(Register_File_r_out_1), .en(d_ff_2_q), .Q(valA_q), .clk(clock_1_out));  // open: clr
  Register valB (.D(Register_File_r_out_2), .en(d_ff_2_q), .Q(valB_q), .clk(clock_1_out));  // open: clr
  D_Flip_Flop d_ff_3 (.clk(clock_1_out), .D(d_ff_2_q), .Q(d_ff_3_q));  // open: Qn, preset, en, reset
  Multiplexer #(.width(8), .enable("false")) multiplexer_3 (
    .in0(valC_q), .in1(valA_q), .out(multiplexer_3_out), .sel(mycirc_1_out_4));
  ALU ALU (.A(multiplexer_3_out), .B(valB_q), .ALU_fun(mycirc_1_out_7), .val_E(ALU_val_e));
  D_Flip_Flop d_ff_4 (.clk(clock_1_out), .D(d_ff_3_q), .Q(d_ff_4_q));  // open: Qn, preset, en, reset
  Register valE (.D(ALU_val_e), .en(d_ff_3_q), .Q(valE_q), .clk(clock_1_out));  // open: clr
  Multiplexer #(.width(8), .enable("false")) multiplexer_4 (
    .in0(valE_q), .in1(valA_q), .out(multiplexer_4_out), .sel(mycirc_1_out_5));
  RAM #(.bus("separate")) ram_1 (
    .addr(multiplexer_4_out), .din(valE_q), .data(ram_1_data), .str(mycirc_1_out_5), .clk(clock_1_out),
    .ld(mycirc_1_out_6));  // open: sel, clr
  Register valM (.D(ram_1_data), .en(d_ff_4_q), .Q(valM_q), .clk(clock_1_out));  // open: clr
  D_Flip_Flop d_ff_5 (.clk(clock_1_out), .D(d_ff_4_q), .Q(d_ff_5_q));  // open: Qn, preset, en, reset
  Multiplexer #(.width(8), .enable("false")) multiplexer_5 (
    .in0(valE_q), .in1(valP_q), .out(multiplexer_5_out), .sel(mycirc_1_out_8));

  // Notes on the sheet:
  //   Fetch
  //   contents of rom_1 (hex, n*v repeats v):
  //   2110 2220 2330 2440 2490 23a0 22b0 21c0 3150 3260 3370 3480 1590 16a0 17b0 18c0 4090 41a0 42b0 43c0
  //   f000
  //   Decode
  //   Write Back
  //   Execute
  //   Memory
  //   PC Update
endmodule

module Register_File (
  input  [7:0] w_data,
  input  [3:0] r_addr_1,
  input  e,
  input  e_2,
  input  [3:0] w_addr,
  input  in_6,
  input  e_3,
  input  [3:0] r_addr_1_2,
  output [7:0] r_out_1,
  output [7:0] r_out_2
);

  wire demultiplexer_1_out0, demultiplexer_1_out1, demultiplexer_1_out2, demultiplexer_1_out3,
       demultiplexer_1_out4, demultiplexer_1_out5, demultiplexer_1_out6, demultiplexer_1_out7,
       demultiplexer_1_out8, demultiplexer_1_out9, demultiplexer_1_out10, demultiplexer_1_out11,
       demultiplexer_1_out12, demultiplexer_1_out13, demultiplexer_1_out14, demultiplexer_1_out15,
       demultiplexer_2_out0, demultiplexer_2_out1, demultiplexer_2_out2, demultiplexer_2_out3,
       demultiplexer_2_out4, demultiplexer_2_out5, demultiplexer_2_out6, demultiplexer_2_out7,
       demultiplexer_2_out8, demultiplexer_2_out9, demultiplexer_2_out10, demultiplexer_2_out11,
       demultiplexer_2_out12, demultiplexer_2_out13, demultiplexer_2_out14, demultiplexer_2_out15,
       demultiplexer_3_out0, demultiplexer_3_out1, demultiplexer_3_out2, demultiplexer_3_out3,
       demultiplexer_3_out4, demultiplexer_3_out5, demultiplexer_3_out6, demultiplexer_3_out7,
       demultiplexer_3_out8, demultiplexer_3_out9, demultiplexer_3_out10, demultiplexer_3_out11,
       demultiplexer_3_out12, demultiplexer_3_out13, demultiplexer_3_out14, demultiplexer_3_out15;
  wire [7:0] register_1_q, register_2_q, register_3_q, register_4_q, register_5_q, register_6_q,
       register_7_q, register_8_q, register_9_q, register_10_q, register_11_q, register_12_q, register_13_q,
       register_14_q, register_15_q, register_16_q;

  Demultiplexer #(.select(4)) demultiplexer_1 (
    .out0(demultiplexer_1_out0), .out1(demultiplexer_1_out1), .out2(demultiplexer_1_out2),
    .out3(demultiplexer_1_out3), .out4(demultiplexer_1_out4), .out5(demultiplexer_1_out5),
    .out6(demultiplexer_1_out6), .out7(demultiplexer_1_out7), .out8(demultiplexer_1_out8),
    .out9(demultiplexer_1_out9), .out10(demultiplexer_1_out10), .out11(demultiplexer_1_out11),
    .out12(demultiplexer_1_out12), .out13(demultiplexer_1_out13), .out14(demultiplexer_1_out14),
    .out15(demultiplexer_1_out15), .in(1'b1), .sel(w_addr), .en(e_2));
  Register register_1 (.D(w_data), .en(demultiplexer_1_out0), .Q(register_1_q), .clk(in_6));  // open: clr
  Register register_2 (.D(w_data), .en(demultiplexer_1_out1), .Q(register_2_q), .clk(in_6));  // open: clr
  Register register_3 (.D(w_data), .en(demultiplexer_1_out2), .Q(register_3_q), .clk(in_6));  // open: clr
  Register register_4 (.D(w_data), .en(demultiplexer_1_out3), .Q(register_4_q), .clk(in_6));  // open: clr
  Register register_5 (.D(w_data), .en(demultiplexer_1_out4), .Q(register_5_q), .clk(in_6));  // open: clr
  Register register_6 (.D(w_data), .en(demultiplexer_1_out5), .Q(register_6_q), .clk(in_6));  // open: clr
  Register register_7 (.D(w_data), .en(demultiplexer_1_out6), .Q(register_7_q), .clk(in_6));  // open: clr
  Register register_8 (.D(w_data), .en(demultiplexer_1_out7), .Q(register_8_q), .clk(in_6));  // open: clr
  Register register_9 (.D(w_data), .en(demultiplexer_1_out8), .Q(register_9_q), .clk(in_6));  // open: clr
  Register register_10 (.D(w_data), .en(demultiplexer_1_out9), .Q(register_10_q), .clk(in_6));  // open: clr
  Register register_11 (.D(w_data), .en(demultiplexer_1_out10), .Q(register_11_q), .clk(in_6));  // open: clr
  Register register_12 (.D(w_data), .en(demultiplexer_1_out11), .Q(register_12_q), .clk(in_6));  // open: clr
  Register register_13 (.D(w_data), .en(demultiplexer_1_out12), .Q(register_13_q), .clk(in_6));  // open: clr
  Register register_14 (.D(w_data), .en(demultiplexer_1_out13), .Q(register_14_q), .clk(in_6));  // open: clr
  Register register_15 (.D(w_data), .en(demultiplexer_1_out14), .Q(register_15_q), .clk(in_6));  // open: clr
  Register register_16 (.D(w_data), .en(demultiplexer_1_out15), .Q(register_16_q), .clk(in_6));  // open: clr
  assign r_out_1 = demultiplexer_2_out0 ? register_1_q : 8'bz;  // Controlled_Buffer controlled_buffer_1
  assign r_out_2 = demultiplexer_3_out0 ? register_1_q : 8'bz;  // Controlled_Buffer controlled_buffer_2
  assign r_out_1 = demultiplexer_2_out1 ? register_2_q : 8'bz;  // Controlled_Buffer controlled_buffer_3
  assign r_out_2 = demultiplexer_3_out1 ? register_2_q : 8'bz;  // Controlled_Buffer controlled_buffer_4
  assign r_out_1 = demultiplexer_2_out2 ? register_3_q : 8'bz;  // Controlled_Buffer controlled_buffer_5
  assign r_out_2 = demultiplexer_3_out2 ? register_3_q : 8'bz;  // Controlled_Buffer controlled_buffer_6
  assign r_out_1 = demultiplexer_2_out3 ? register_4_q : 8'bz;  // Controlled_Buffer controlled_buffer_7
  assign r_out_2 = demultiplexer_3_out3 ? register_4_q : 8'bz;  // Controlled_Buffer controlled_buffer_8
  assign r_out_1 = demultiplexer_2_out4 ? register_5_q : 8'bz;  // Controlled_Buffer controlled_buffer_9
  assign r_out_2 = demultiplexer_3_out4 ? register_5_q : 8'bz;  // Controlled_Buffer controlled_buffer_10
  assign r_out_1 = demultiplexer_2_out5 ? register_6_q : 8'bz;  // Controlled_Buffer controlled_buffer_11
  assign r_out_2 = demultiplexer_3_out5 ? register_6_q : 8'bz;  // Controlled_Buffer controlled_buffer_12
  assign r_out_1 = demultiplexer_2_out6 ? register_7_q : 8'bz;  // Controlled_Buffer controlled_buffer_13
  assign r_out_2 = demultiplexer_3_out6 ? register_7_q : 8'bz;  // Controlled_Buffer controlled_buffer_14
  assign r_out_1 = demultiplexer_2_out7 ? register_8_q : 8'bz;  // Controlled_Buffer controlled_buffer_15
  assign r_out_2 = demultiplexer_3_out7 ? register_8_q : 8'bz;  // Controlled_Buffer controlled_buffer_16
  assign r_out_1 = demultiplexer_2_out8 ? register_9_q : 8'bz;  // Controlled_Buffer controlled_buffer_17
  assign r_out_2 = demultiplexer_3_out8 ? register_9_q : 8'bz;  // Controlled_Buffer controlled_buffer_18
  assign r_out_1 = demultiplexer_2_out9 ? register_10_q : 8'bz;  // Controlled_Buffer controlled_buffer_19
  assign r_out_2 = demultiplexer_3_out9 ? register_10_q : 8'bz;  // Controlled_Buffer controlled_buffer_20
  assign r_out_1 = demultiplexer_2_out10 ? register_11_q : 8'bz;  // Controlled_Buffer controlled_buffer_21
  assign r_out_2 = demultiplexer_3_out10 ? register_11_q : 8'bz;  // Controlled_Buffer controlled_buffer_22
  assign r_out_1 = demultiplexer_2_out11 ? register_12_q : 8'bz;  // Controlled_Buffer controlled_buffer_23
  assign r_out_2 = demultiplexer_3_out11 ? register_12_q : 8'bz;  // Controlled_Buffer controlled_buffer_24
  assign r_out_1 = demultiplexer_2_out12 ? register_13_q : 8'bz;  // Controlled_Buffer controlled_buffer_25
  assign r_out_2 = demultiplexer_3_out12 ? register_13_q : 8'bz;  // Controlled_Buffer controlled_buffer_26
  assign r_out_1 = demultiplexer_2_out13 ? register_14_q : 8'bz;  // Controlled_Buffer controlled_buffer_27
  assign r_out_2 = demultiplexer_3_out13 ? register_14_q : 8'bz;  // Controlled_Buffer controlled_buffer_28
  assign r_out_1 = demultiplexer_2_out14 ? register_15_q : 8'bz;  // Controlled_Buffer controlled_buffer_29
  assign r_out_2 = demultiplexer_3_out14 ? register_15_q : 8'bz;  // Controlled_Buffer controlled_buffer_30
  assign r_out_1 = demultiplexer_2_out15 ? register_16_q : 8'bz;  // Controlled_Buffer controlled_buffer_31
  assign r_out_2 = demultiplexer_3_out15 ? register_16_q : 8'bz;  // Controlled_Buffer controlled_buffer_32
  Demultiplexer #(.select(4)) demultiplexer_2 (
    .out0(demultiplexer_2_out0), .out1(demultiplexer_2_out1), .out2(demultiplexer_2_out2),
    .out3(demultiplexer_2_out3), .out4(demultiplexer_2_out4), .out5(demultiplexer_2_out5),
    .out6(demultiplexer_2_out6), .out7(demultiplexer_2_out7), .out8(demultiplexer_2_out8),
    .out9(demultiplexer_2_out9), .out10(demultiplexer_2_out10), .out11(demultiplexer_2_out11),
    .out12(demultiplexer_2_out12), .out13(demultiplexer_2_out13), .out14(demultiplexer_2_out14),
    .out15(demultiplexer_2_out15), .in(1'b1), .sel(r_addr_1), .en(e));
  Demultiplexer #(.select(4)) demultiplexer_3 (
    .out0(demultiplexer_3_out0), .out1(demultiplexer_3_out1), .out2(demultiplexer_3_out2),
    .out3(demultiplexer_3_out3), .out4(demultiplexer_3_out4), .out5(demultiplexer_3_out5),
    .out6(demultiplexer_3_out6), .out7(demultiplexer_3_out7), .out8(demultiplexer_3_out8),
    .out9(demultiplexer_3_out9), .out10(demultiplexer_3_out10), .out11(demultiplexer_3_out11),
    .out12(demultiplexer_3_out12), .out13(demultiplexer_3_out13), .out14(demultiplexer_3_out14),
    .out15(demultiplexer_3_out15), .in(1'b1), .sel(r_addr_1_2), .en(e_3));
endmodule

module ALU (
  input  [7:0] A,
  input  [7:0] B,
  input  [2:0] ALU_fun,
  output [7:0] val_E
);

  wire [7:0] multiplexer_1_out, multiplexer_2_out, negator_1_out;

  Negator negator_1 (.in(A), .out(negator_1_out));
  Multiplexer #(.width(8)) multiplexer_1 (
    .in0(B), .in1({8{1'b0}}), .out(multiplexer_1_out), .sel(ALU_fun[2]));  // open: en
  Multiplexer #(.select(2), .width(8)) multiplexer_2 (
    .in0({8{1'b0}}), .in1(A), .in2(negator_1_out), .out(multiplexer_2_out), .sel(ALU_fun[1:0]));  // open: in3, en
  Adder adder_1 (.a(multiplexer_2_out), .b(multiplexer_1_out), .out(val_E));  // open: cin, cout
endmodule

module myCirc (
  input  [3:0] in_1,
  output [1:0] out_2,
  output out_3,
  output out_4,
  output out_5,
  output out_6,
  output [2:0] out_7,
  output out_8
);

  wire and_1_out, and_2_out, and_3_out, and_5_out, and_6_out, and_9_out, and_10_out, and_11_out, and_12_out;

  and and_1 (and_1_out, in_1[0], ~in_1[1], ~in_1[3]);  // AND_Gate
  and and_2 (and_2_out, in_1[0], ~in_1[2], ~in_1[3]);  // AND_Gate
  and and_3 (and_3_out, in_1[0], in_1[1], in_1[2], ~in_1[3]);  // AND_Gate
  and and_4 (out_3, in_1[0], ~in_1[1], in_1[2], ~in_1[3]);  // AND_Gate
  and and_5 (and_5_out, in_1[0], ~in_1[2], ~in_1[3]);  // AND_Gate
  and and_6 (and_6_out, ~in_1[1], in_1[2], ~in_1[3]);  // AND_Gate
  and and_7 (out_5, ~in_1[0], ~in_1[1], in_1[2], ~in_1[3]);  // AND_Gate
  and and_8 (out_6, in_1[0], ~in_1[1], in_1[2], ~in_1[3]);  // AND_Gate
  and and_9 (and_9_out, in_1[0], in_1[1], ~in_1[2], ~in_1[3]);  // AND_Gate
  and and_10 (and_10_out, ~in_1[2], ~in_1[3]);  // AND_Gate
  and and_11 (and_11_out, ~in_1[1], in_1[2], ~in_1[3]);  // AND_Gate
  and and_12 (and_12_out, in_1[1], in_1[2], ~in_1[3]);  // AND_Gate
  or or_1 (out_2[0], and_1_out, and_2_out);
  or or_2 (out_2[1], and_3_out, and_12_out);
  or or_3 (out_7[0], and_6_out, and_9_out);
  or or_4 (out_8, and_10_out, and_11_out);
  or or_5 (out_4, and_5_out, and_3_out, and_6_out);

  assign out_7[2:1] = {out_3, 1'b0};
endmodule
