// Logisim project mainCPU_copy.circ as structural Verilog: 4 circuits, main circuit main
module main (
);

  wire and_1_out, and_2_out, button_1_out, clock_1_out, d_ff_1_q, d_ff_2_q, d_ff_3_q, d_ff_4_q, d_ff_5_q,
       d_ff_6_q, d_ff_7_q, not_1_out, not_2_out, not_3_out, or_1_out, register_1_q, xnor_1_out;
  wire [0:0] icode_2_pc_mux;
  wire [1:0] icode_2_mem_addr_mux, icode_2_mem_data_mux;
  wire [2:0] icode_2_wb_addr_mux;
  wire [3:0] icode_2_ex_val_mux, iCode_q, multiplexer_1_out, rA_q, rB_q;
  wire [7:0] ALU_val_e, counter_1_q, multiplexer_2_out, multiplexer_3_out, multiplexer_4_out,
       multiplexer_5_out, multiplexer_6_out, PC_q, ram_1_data, Register_File_r_out_1, Register_File_r_out_2,
       valA_q, valB_q, valC_q, valE_q, valM_q, valP_q;
  wire [15:0] rom_1_data;

  Clock clock_1 (.out(clock_1_out));
  Button button_1 (.out(button_1_out));
  Register #(.width(1)) register_1 (.D(and_1_out), .Q(register_1_q), .clk(clock_1_out), .clr(and_2_out));  // open: en
  not not_1 (not_1_out, register_1_q);
  Register PC (.D(multiplexer_6_out), .en(not_1_out), .Q(PC_q), .clk(clock_1_out), .clr(and_2_out));
  D_Flip_Flop d_ff_1 (.clk(clock_1_out), .D(button_1_out), .Q(d_ff_1_q));  // open: Qn, preset, en, reset
  and and_1 (and_1_out, iCode_q[3], iCode_q[2], iCode_q[1], iCode_q[0]);
  not not_2 (not_2_out, d_ff_1_q);
  or or_1 (or_1_out, and_2_out, d_ff_7_q, xnor_1_out);
  and and_2 (and_2_out, not_2_out, button_1_out);
  ROM #(.dataWidth(16)) rom_1 (.addr(PC_q), .data(rom_1_data));  // open: sel
  D_Flip_Flop d_ff_2 (.clk(clock_1_out), .D(or_1_out), .Q(d_ff_2_q));  // open: Qn, preset, en, reset
  NotExactlyOne xnor_1 (
    .out(xnor_1_out), .in0(d_ff_2_q), .in1(d_ff_3_q), .in2(d_ff_4_q), .in3(d_ff_5_q), .in4(d_ff_6_q),
    .in5(d_ff_7_q));
  Counter counter_1 (.D(PC_q), .Q(counter_1_q), .clk(d_ff_7_q), .clr(and_2_out));  // open: load, count, carry
  Register #(.width(4)) iCode (.D(rom_1_data[15:12]), .Q(iCode_q), .clk(clock_1_out));  // open: en, clr
  Register #(.width(4)) rA (.D(rom_1_data[11:8]), .Q(rA_q), .clk(clock_1_out));  // open: en, clr
  Register #(.width(4)) rB (.D(rom_1_data[7:4]), .Q(rB_q), .clk(clock_1_out));  // open: en, clr
  Register valC (.D({rom_1_data[3:0], rom_1_data[7:4]}), .Q(valC_q), .clk(clock_1_out));  // open: en, clr
  D_Flip_Flop d_ff_3 (.clk(clock_1_out), .D(d_ff_2_q), .Q(d_ff_3_q), .reset(xnor_1_out));  // open: Qn, preset, en
  Register valP (.D(counter_1_q), .Q(valP_q), .clk(clock_1_out), .clr(and_2_out));  // open: en
  Multiplexer #(.width(4), .enable("false")) multiplexer_1 (
    .in0(rA_q), .in1(rB_q), .out(multiplexer_1_out), .sel(icode_2_wb_addr_mux[0]));
  Multiplexer #(.width(8), .enable("false")) multiplexer_2 (
    .in0(valE_q), .in1(valM_q), .out(multiplexer_2_out), .sel(icode_2_wb_addr_mux[2]));
  Register_File Register_File (
    .w_data(multiplexer_2_out), .e_2(d_ff_7_q), .w_addr(multiplexer_1_out), .e(d_ff_3_q), .r_addr_1(rA_q),
    .r_out_1(Register_File_r_out_1), .r_out_2(Register_File_r_out_2), .e_3(d_ff_3_q), .r_addr_1_2(rB_q),
    .in_6(clock_1_out));
  D_Flip_Flop d_ff_4 (.clk(clock_1_out), .D(d_ff_3_q), .Q(d_ff_4_q), .reset(xnor_1_out));  // open: Qn, preset, en
  Register valA (.D(Register_File_r_out_1), .en(d_ff_4_q), .Q(valA_q), .clk(clock_1_out));  // open: clr
  Register valB (.D(Register_File_r_out_2), .en(d_ff_4_q), .Q(valB_q), .clk(clock_1_out));  // open: clr
  iCode icode_2 (
    .in_1(iCode_q), .wb_addr_mux(icode_2_wb_addr_mux[0]), .wb_val_mux(icode_2_wb_addr_mux[2]),
    .ex_val_mux(icode_2_ex_val_mux[0]), .ex_alu_mux(icode_2_ex_val_mux[3:2]),
    .mem_addr_mux(icode_2_mem_addr_mux[0]), .mem_data_mux(icode_2_mem_data_mux[0]),
    .pc_mux(icode_2_pc_mux[0]), .mem_data_e(icode_2_mem_data_mux[1]), .mem_addr_e(icode_2_mem_addr_mux[1]));
  D_Flip_Flop d_ff_5 (.clk(clock_1_out), .D(d_ff_4_q), .Q(d_ff_5_q), .reset(xnor_1_out));  // open: Qn, preset, en
  Multiplexer #(.width(8), .enable("false")) multiplexer_3 (
    .in0(valC_q), .in1(valA_q), .out(multiplexer_3_out), .sel(icode_2_ex_val_mux[0]));
  ALU ALU (.A(multiplexer_3_out), .B(valB_q), .ALU_fun(icode_2_ex_val_mux[3:2]), .val_E(ALU_val_e));
  D_Flip_Flop d_ff_6 (.clk(clock_1_out), .D(d_ff_5_q), .Q(d_ff_6_q), .reset(xnor_1_out));  // open: Qn, preset, en
  Register valE (.D(ALU_val_e), .en(d_ff_5_q), .Q(valE_q), .clk(clock_1_out));  // open: clr
  Multiplexer #(.width(8), .enable("false")) multiplexer_4 (
    .in0(valE_q), .in1(valA_q), .out(multiplexer_4_out), .sel(icode_2_mem_addr_mux[0]));
  Multiplexer #(.width(8), .enable("false")) multiplexer_5 (
    .in0(valE_q), .in1(valA_q), .out(multiplexer_5_out), .sel(icode_2_mem_data_mux[0]));
  not not_3 (not_3_out, icode_2_mem_data_mux[1]);
  Register valM (.D(ram_1_data), .en(d_ff_6_q), .Q(valM_q), .clk(clock_1_out));  // open: clr
  RAM #(.bus("separate")) ram_1 (
    .addr(multiplexer_4_out), .din(multiplexer_5_out), .data(ram_1_data), .sel(icode_2_mem_addr_mux[1]),
    .clk(clock_1_out), .ld(not_3_out));  // open: str, clr
  D_Flip_Flop d_ff_7 (.clk(clock_1_out), .D(d_ff_6_q), .Q(d_ff_7_q), .reset(xnor_1_out));  // open: Qn, preset, en
  Multiplexer #(.width(8), .enable("false")) multiplexer_6 (
    .in0(valE_q), .in1(valP_q), .out(multiplexer_6_out), .sel(icode_2_pc_mux[0]));

  // Notes on the sheet:
  //   Fetch
  //   contents of rom_1 (hex, n*v repeats v):
  //   2110 2220 2330 2440 2940 2a30 2b20 2c10 3150 3260 3370 3480 1590 16a0 17b0 18c0 4090 41a0 42b0 43c0
  //   f000
  //   Decode
  //   Write Back
  //   Execute
  //   Memory
  //   PC Update
endmodule

module Register_File (
  input  [7:0] w_data,
  input  [3:0] r_addr_1,
  input  e,
  input  e_2,
  input  [3:0] w_addr,
  input  in_6,
  input  e_3,
  input  [3:0] r_addr_1_2,
  output [7:0] r_out_1,
  output [7:0] r_out_2
);

  wire and_1_out, and_2_out, and_3_out, and_4_out, and_5_out, and_6_out, and_7_out, and_8_out, and_9_out,
       and_10_out, and_11_out, and_12_out, and_13_out, and_14_out, and_15_out, and_16_out,
       demultiplexer_1_out0, demultiplexer_1_out1, demultiplexer_1_out2, demultiplexer_1_out3,
       demultiplexer_1_out4, demultiplexer_1_out5, demultiplexer_1_out6, demultiplexer_1_out7,
       demultiplexer_1_out8, demultiplexer_1_out9, demultiplexer_1_out10, demultiplexer_1_out11,
       demultiplexer_1_out12, demultiplexer_1_out13, demultiplexer_1_out14, demultiplexer_1_out15,
       demultiplexer_2_out0, demultiplexer_2_out1, demultiplexer_2_out2, demultiplexer_2_out3,
       demultiplexer_2_out4, demultiplexer_2_out5, demultiplexer_2_out6, demultiplexer_2_out7,
       demultiplexer_2_out8, demultiplexer_2_out9, demultiplexer_2_out10, demultiplexer_2_out11,
       demultiplexer_2_out12, demultiplexer_2_out13, demultiplexer_2_out14, demultiplexer_2_out15,
       demultiplexer_3_out0, demultiplexer_3_out1, demultiplexer_3_out2, demultiplexer_3_out3,
       demultiplexer_3_out4, demultiplexer_3_out5, demultiplexer_3_out6, demultiplexer_3_out7,
       demultiplexer_3_out8, demultiplexer_3_out9, demultiplexer_3_out10, demultiplexer_3_out11,
       demultiplexer_3_out12, demultiplexer_3_out13, demultiplexer_3_out14, demultiplexer_3_out15;
  wire [7:0] register_1_q, register_2_q, register_3_q, register_4_q, register_5_q, register_6_q,
       register_7_q, register_8_q, register_9_q, register_10_q, register_11_q, register_12_q, register_13_q,
       register_14_q, register_15_q, register_16_q;

  Demultiplexer #(.select(4)) demultiplexer_1 (
    .out0(demultiplexer_1_out0), .out1(demultiplexer_1_out1), .out2(demultiplexer_1_out2),
    .out3(demultiplexer_1_out3), .out4(demultiplexer_1_out4), .out5(demultiplexer_1_out5),
    .out6(demultiplexer_1_out6), .out7(demultiplexer_1_out7), .out8(demultiplexer_1_out8),
    .out9(demultiplexer_1_out9), .out10(demultiplexer_1_out10), .out11(demultiplexer_1_out11),
    .out12(demultiplexer_1_out12), .out13(demultiplexer_1_out13), .out14(demultiplexer_1_out14),
    .out15(demultiplexer_1_out15), .in(1'b1), .sel(w_addr));  // open: en
  and and_1 (and_1_out, demultiplexer_1_out0, e_2);
  and and_2 (and_2_out, demultiplexer_1_out1, e_2);
  and and_3 (and_3_out, demultiplexer_1_out2, e_2);
  and and_4 (and_4_out, demultiplexer_1_out3, e_2);
  and and_5 (and_5_out, demultiplexer_1_out4, e_2);
  and and_6 (and_6_out, demultiplexer_1_out5, e_2);
  and and_7 (and_7_out, demultiplexer_1_out6, e_2);
  and and_8 (and_8_out, demultiplexer_1_out7, e_2);
  and and_9 (and_9_out, demultiplexer_1_out8, e_2);
  and and_10 (and_10_out, demultiplexer_1_out9, e_2);
  and and_11 (and_11_out, demultiplexer_1_out10, e_2);
  and and_12 (and_12_out, demultiplexer_1_out11, e_2);
  and and_13 (and_13_out, demultiplexer_1_out12, e_2);
  and and_14 (and_14_out, demultiplexer_1_out13, e_2);
  and and_15 (and_15_out, demultiplexer_1_out14, e_2);
  and and_16 (and_16_out, demultiplexer_1_out15, e_2);
  Register register_1 (.D(w_data), .en(and_1_out), .Q(register_1_q), .clk(in_6));  // open: clr
  Register register_2 (.D(w_data), .en(and_2_out), .Q(register_2_q), .clk(in_6));  // open: clr
  Register register_3 (.D(w_data), .en(and_3_out), .Q(register_3_q), .clk(in_6));  // open: clr
  Register register_4 (.D(w_data), .en(and_4_out), .Q(register_4_q), .clk(in_6));  // open: clr
  Register register_5 (.D(w_data), .en(and_5_out), .Q(register_5_q), .clk(in_6));  // open: clr
  Register register_6 (.D(w_data), .en(and_6_out), .Q(register_6_q), .clk(in_6));  // open: clr
  Register register_7 (.D(w_data), .en(and_7_out), .Q(register_7_q), .clk(in_6));  // open: clr
  Register register_8 (.D(w_data), .en(and_8_out), .Q(register_8_q), .clk(in_6));  // open: clr
  Register register_9 (.D(w_data), .en(and_9_out), .Q(register_9_q), .clk(in_6));  // open: clr
  Register register_10 (.D(w_data), .en(and_10_out), .Q(register_10_q), .clk(in_6));  // open: clr
  Register register_11 (.D(w_data), .en(and_11_out), .Q(register_11_q), .clk(in_6));  // open: clr
  Register register_12 (.D(w_data), .en(and_12_out), .Q(register_12_q), .clk(in_6));  // open: clr
  Register register_13 (.D(w_data), .en(and_13_out), .Q(register_13_q), .clk(in_6));  // open: clr
  Register register_14 (.D(w_data), .en(and_14_out), .Q(register_14_q), .clk(in_6));  // open: clr
  Register register_15 (.D(w_data), .en(and_15_out), .Q(register_15_q), .clk(in_6));  // open: clr
  Register register_16 (.D(w_data), .en(and_16_out), .Q(register_16_q), .clk(in_6));  // open: clr
  assign r_out_1 = demultiplexer_2_out0 ? register_1_q : 8'bz;  // Controlled_Buffer controlled_buffer_1
  assign r_out_2 = demultiplexer_3_out0 ? register_1_q : 8'bz;  // Controlled_Buffer controlled_buffer_2
  assign r_out_1 = demultiplexer_2_out1 ? register_2_q : 8'bz;  // Controlled_Buffer controlled_buffer_3
  assign r_out_2 = demultiplexer_3_out1 ? register_2_q : 8'bz;  // Controlled_Buffer controlled_buffer_4
  assign r_out_1 = demultiplexer_2_out2 ? register_3_q : 8'bz;  // Controlled_Buffer controlled_buffer_5
  assign r_out_2 = demultiplexer_3_out2 ? register_3_q : 8'bz;  // Controlled_Buffer controlled_buffer_6
  assign r_out_1 = demultiplexer_2_out3 ? register_4_q : 8'bz;  // Controlled_Buffer controlled_buffer_7
  assign r_out_2 = demultiplexer_3_out3 ? register_4_q : 8'bz;  // Controlled_Buffer controlled_buffer_8
  assign r_out_1 = demultiplexer_2_out4 ? register_5_q : 8'bz;  // Controlled_Buffer controlled_buffer_9
  assign r_out_2 = demultiplexer_3_out4 ? register_5_q : 8'bz;  // Controlled_Buffer controlled_buffer_10
  assign r_out_1 = demultiplexer_2_out5 ? register_6_q : 8'bz;  // Controlled_Buffer controlled_buffer_11
  assign r_out_2 = demultiplexer_3_out5 ? register_6_q : 8'bz;  // Controlled_Buffer controlled_buffer_12
  assign r_out_1 = demultiplexer_2_out6 ? register_7_q : 8'bz;  // Controlled_Buffer controlled_buffer_13
  assign r_out_2 = demultiplexer_3_out6 ? register_7_q : 8'bz;  // Controlled_Buffer controlled_buffer_14
  assign r_out_1 = demultiplexer_2_out7 ? register_8_q : 8'bz;  // Controlled_Buffer controlled_buffer_15
  assign r_out_2 = demultiplexer_3_out7 ? register_8_q : 8'bz;  // Controlled_Buffer controlled_buffer_16
  assign r_out_1 = demultiplexer_2_out8 ? register_9_q : 8'bz;  // Controlled_Buffer controlled_buffer_17
  assign r_out_2 = demultiplexer_3_out8 ? register_9_q : 8'bz;  // Controlled_Buffer controlled_buffer_18
  assign r_out_1 = demultiplexer_2_out9 ? register_10_q : 8'bz;  // Controlled_Buffer controlled_buffer_19
  assign r_out_2 = demultiplexer_3_out9 ? register_10_q : 8'bz;  // Controlled_Buffer controlled_buffer_20
  assign r_out_1 = demultiplexer_2_out10 ? register_11_q : 8'bz;  // Controlled_Buffer controlled_buffer_21
  assign r_out_2 = demultiplexer_3_out10 ? register_11_q : 8'bz;  // Controlled_Buffer controlled_buffer_22
  assign r_out_1 = demultiplexer_2_out11 ? register_12_q : 8'bz;  // Controlled_Buffer controlled_buffer_23
  assign r_out_2 = demultiplexer_3_out11 ? register_12_q : 8'bz;  // Controlled_Buffer controlled_buffer_24
  assign r_out_1 = demultiplexer_2_out12 ? register_13_q : 8'bz;  // Controlled_Buffer controlled_buffer_25
  assign r_out_2 = demultiplexer_3_out12 ? register_13_q : 8'bz;  // Controlled_Buffer controlled_buffer_26
  assign r_out_1 = demultiplexer_2_out13 ? register_14_q : 8'bz;  // Controlled_Buffer controlled_buffer_27
  assign r_out_2 = demultiplexer_3_out13 ? register_14_q : 8'bz;  // Controlled_Buffer controlled_buffer_28
  assign r_out_1 = demultiplexer_2_out14 ? register_15_q : 8'bz;  // Controlled_Buffer controlled_buffer_29
  assign r_out_2 = demultiplexer_3_out14 ? register_15_q : 8'bz;  // Controlled_Buffer controlled_buffer_30
  assign r_out_1 = demultiplexer_2_out15 ? register_16_q : 8'bz;  // Controlled_Buffer controlled_buffer_31
  assign r_out_2 = demultiplexer_3_out15 ? register_16_q : 8'bz;  // Controlled_Buffer controlled_buffer_32
  Demultiplexer #(.select(4)) demultiplexer_2 (
    .out0(demultiplexer_2_out0), .out1(demultiplexer_2_out1), .out2(demultiplexer_2_out2),
    .out3(demultiplexer_2_out3), .out4(demultiplexer_2_out4), .out5(demultiplexer_2_out5),
    .out6(demultiplexer_2_out6), .out7(demultiplexer_2_out7), .out8(demultiplexer_2_out8),
    .out9(demultiplexer_2_out9), .out10(demultiplexer_2_out10), .out11(demultiplexer_2_out11),
    .out12(demultiplexer_2_out12), .out13(demultiplexer_2_out13), .out14(demultiplexer_2_out14),
    .out15(demultiplexer_2_out15), .in(1'b1), .sel(r_addr_1), .en(e));
  Demultiplexer #(.select(4)) demultiplexer_3 (
    .out0(demultiplexer_3_out0), .out1(demultiplexer_3_out1), .out2(demultiplexer_3_out2),
    .out3(demultiplexer_3_out3), .out4(demultiplexer_3_out4), .out5(demultiplexer_3_out5),
    .out6(demultiplexer_3_out6), .out7(demultiplexer_3_out7), .out8(demultiplexer_3_out8),
    .out9(demultiplexer_3_out9), .out10(demultiplexer_3_out10), .out11(demultiplexer_3_out11),
    .out12(demultiplexer_3_out12), .out13(demultiplexer_3_out13), .out14(demultiplexer_3_out14),
    .out15(demultiplexer_3_out15), .in(1'b1), .sel(r_addr_1_2), .en(e_3));
endmodule

module ALU (
  input  [7:0] A,
  input  [7:0] B,
  input  [1:0] ALU_fun,
  output [7:0] val_E
);

  wire [7:0] multiplexer_1_out, negator_1_out;

  Negator negator_1 (.in(A), .out(negator_1_out));
  Multiplexer #(.select(2), .width(8)) multiplexer_1 (
    .in0({8{1'b0}}), .in1(A), .in2(negator_1_out), .out(multiplexer_1_out), .sel(ALU_fun));  // open: in3, en
  Adder adder_1 (.a(multiplexer_1_out), .b(B), .out(val_E));  // open: cin, cout
endmodule

module iCode (
  input  [3:0] in_1,
  output mem_addr_mux,
  output mem_addr_e,
  output mem_data_mux,
  output mem_data_e,
  output pc_mux,
  output wb_addr_mux,
  output wb_val_mux,
  output ex_val_mux,
  output [1:0] ex_alu_mux
);

  wire decoder_1_out1, decoder_1_out2, decoder_1_out3, decoder_1_out6, decoder_1_out7, or_2_out, or_3_out,
       or_6_out, wb_addr_e_out, wb_val_e_out;

  Decoder #(.select(4)) decoder_1 (
    .out1(decoder_1_out1), .out2(decoder_1_out2), .out3(decoder_1_out3), .out4(mem_data_e),
    .out5(mem_addr_mux), .out6(decoder_1_out6), .out7(decoder_1_out7), .sel(in_1));  // open: out0, out8, out9, out10, out11, out12, out13, out14, out15, en
  not not_1 (wb_addr_mux, decoder_1_out2);
  or wb_addr_e (wb_addr_e_out, decoder_1_out1, decoder_1_out2, decoder_1_out3, mem_addr_mux);
  or wb_val_e (wb_val_e_out, decoder_1_out1, decoder_1_out2, decoder_1_out3, mem_addr_mux);
  or or_1 (ex_val_mux, decoder_1_out1, decoder_1_out3, mem_data_e, mem_addr_mux);
  or or_2 (or_2_out, decoder_1_out1, decoder_1_out2, decoder_1_out3, mem_data_e, mem_addr_mux, decoder_1_out6, decoder_1_out7);
  or or_3 (or_3_out, decoder_1_out2, decoder_1_out3, mem_data_e, decoder_1_out6);
  // Priority_Encoder #(.select(2)) priority_encoder_1: pin names not known; wires that end beside it: or_2_out, or_3_out, decoder_1_out1, ex_alu_mux, decoder_1_out7
  // OR_Gate or_4 has open pins: in0=decoder_1_out1, in1=decoder_1_out2, in2=decoder_1_out3, in3=mem_data_e, in4=decoder_1_out6, in5=decoder_1_out7, out=open
  or or_5 (mem_addr_e, mem_data_e, mem_addr_mux);
  nor nor_1 (pc_mux, decoder_1_out6, decoder_1_out7);
  or or_6 (or_6_out, decoder_1_out1, decoder_1_out2, decoder_1_out3, mem_data_e, mem_addr_mux, decoder_1_out6, decoder_1_out7);

  assign mem_data_mux = mem_data_e;
  assign wb_val_mux = mem_addr_mux;
endmodule
